// Logisim project awful.circ as structural Verilog: 1 circuit, main circuit main
module main (
  input  A,
  input  B,
  input  C,
  input  D,
  input  E,
  input  F,
  output V,
  output Q,
  output R,
  output S,
  output T,
  output U
);

  wire nand_1_out, nor_1_out, or_2_out;

  and and_1 (Q, A, B);
  nor nor_1 (nor_1_out, E, T);
  or or_1 (V, Q, or_2_out);
  and and_2 (S, B, D);
  not not_1 (T, nand_1_out);
  or or_2 (or_2_out, C, S);
  not not_2 (R, nor_1_out);
  nand nand_1 (nand_1_out, S, R);
  nor nor_2 (U, R, F);
endmodule
