// Logisim project complex-ff.circ as structural Verilog: 2 circuits, main circuit main
module main (
  input  CLK
);

  wire FF1_qn, FF2_q, FF2_qn, FF3_q, FF3_qn, FF4_qn, FF5_qn, XOR1_out, xor_1_out;

  J_K_Flip_Flop FF1 (.J(FF2_q), .K(FF2_qn), .clk(CLK), .Qn(FF1_qn));  // open: Q, preset, reset
  D_Flip_Flop FF2 (.D(XOR1_out), .clk(CLK), .Q(FF2_q), .Qn(FF2_qn));  // open: preset, reset
  xor XOR1 (XOR1_out, FF2_q, FF1_qn);
  J_K_Flip_Flop FF3 (.J(FF2_q), .K(FF5_qn), .clk(CLK), .Q(FF3_q), .Qn(FF3_qn));  // open: preset, reset
  xor xor_1 (xor_1_out, FF2_q, FF3_q);
  D_Flip_Flop FF4 (.D(FF3_qn), .clk(CLK), .Qn(FF4_qn));  // open: Q, preset, reset
  J_K_Flip_Flop FF5 (.J(xor_1_out), .K(FF4_qn), .clk(CLK), .Qn(FF5_qn));  // open: Q, preset, reset
endmodule

module testbench (
  output [3:0] outval,
  output halt
);

  wire clock_1_out;
  wire [3:0] counter_1_q;

  Clock clock_1 (.out(clock_1_out));
  Counter #(.max('h1f), .width(5)) counter_1 (
    .clk(clock_1_out), .Q({halt, counter_1_q}));  // open: clr, load, up, count, D, carry
  main main_1 (.CLK(outval[0]));
endmodule
