// Logisim project counter_5bit.circ as structural Verilog: 3 circuits, main circuit main
module main (
  input  CLK
);

  wire [4:0] adder_1_out, d_ff_5_q;

  Adder #(.width(5)) adder_1 (.a({5{1'b0}}), .b(d_ff_5_q), .out(adder_1_out), .cin(1'b1));  // open: cout
  D_Flip_Flop d_ff_1 (.D(adder_1_out[4]), .clk(CLK), .Q(d_ff_5_q[4]));  // open: Qn, preset, reset
  D_Flip_Flop d_ff_2 (.D(adder_1_out[3]), .clk(CLK), .Q(d_ff_5_q[3]));  // open: Qn, preset, reset
  D_Flip_Flop d_ff_3 (.D(adder_1_out[2]), .clk(CLK), .Q(d_ff_5_q[2]));  // open: Qn, preset, reset
  D_Flip_Flop d_ff_4 (.D(adder_1_out[1]), .clk(CLK), .Q(d_ff_5_q[1]));  // open: Qn, preset, reset
  D_Flip_Flop d_ff_5 (.D(adder_1_out[0]), .clk(CLK), .Q(d_ff_5_q[0]));  // open: Qn, preset, reset
endmodule

module incrementer (
  input  A0,
  input  A1,
  input  A2,
  input  A3,
  input  A4,
  output Y0,
  output Y1,
  output Y2,
  output Y3,
  output Y4
);

  Adder #(.width(5)) adder_1 (
    .a({5{1'b0}}), .b({A4, A3, A2, A1, A0}), .out({Y4, Y3, Y2, Y1, Y0}), .cin(1'b1));  // open: cout
endmodule

module main_gates (
  input  CLK
);

  wire and_1_out, and_2_out, and_3_out, and_4_out, and_5_out, and_6_out, and_7_out, and_8_out, and_9_out,
       and_10_out, and_11_out, and_12_out, and_13_out, and_14_out, B0_q, B1_q, B2_q, B3_q, B4_q, not_1_out,
       not_2_out, not_3_out, not_4_out, not_5_out, or_1_out, or_2_out, or_3_out, or_4_out;

  not not_1 (not_1_out, B0_q);
  not not_2 (not_2_out, B1_q);
  not not_3 (not_3_out, B2_q);
  not not_4 (not_4_out, B3_q);
  not not_5 (not_5_out, B4_q);
  and and_1 (and_1_out, not_1_out, B1_q);
  and and_2 (and_2_out, B0_q, not_2_out);
  and and_3 (and_3_out, not_1_out, B2_q);
  and and_4 (and_4_out, not_2_out, B2_q);
  and and_5 (and_5_out, B0_q, B1_q, not_3_out);
  and and_6 (and_6_out, not_1_out, B3_q);
  and and_7 (and_7_out, not_2_out, B3_q);
  and and_8 (and_8_out, not_3_out, B3_q);
  and and_9 (and_9_out, B0_q, B1_q, B2_q, not_4_out);
  and and_10 (and_10_out, not_1_out, B4_q);
  and and_11 (and_11_out, not_2_out, B4_q);
  and and_12 (and_12_out, not_3_out, B4_q);
  and and_13 (and_13_out, not_4_out, B4_q);
  and and_14 (and_14_out, B0_q, B1_q, B2_q, B3_q, not_5_out);
  or or_1 (or_1_out, and_1_out, and_2_out);
  or or_2 (or_2_out, and_3_out, and_4_out, and_5_out);
  or or_3 (or_3_out, and_6_out, and_7_out, and_8_out, and_9_out);
  or or_4 (or_4_out, and_10_out, and_11_out, and_12_out, and_13_out, and_14_out);
  D_Flip_Flop B4 (.D(or_4_out), .clk(CLK), .Q(B4_q));  // open: Qn, preset, reset
  D_Flip_Flop B3 (.D(or_3_out), .clk(CLK), .Q(B3_q));  // open: Qn, preset, reset
  D_Flip_Flop B2 (.D(or_2_out), .clk(CLK), .Q(B2_q));  // open: Qn, preset, reset
  D_Flip_Flop B1 (.D(or_1_out), .clk(CLK), .Q(B1_q));  // open: Qn, preset, reset
  D_Flip_Flop B0 (.D(not_1_out), .clk(CLK), .Q(B0_q));  // open: Qn, preset, reset
endmodule
