// Logisim project mutate_me.circ as structural Verilog: 1 circuit, main circuit main
module main (
  input  A,
  input  B,
  input  C,
  input  D,
  output Y0,
  output Y1,
  output Y2,
  output Y3
);

  wire G1_out, G3_out, not_1_out, not_2_out;

  and G1 (G1_out, A, C);
  not not_1 (not_1_out, D);
  and G3 (G3_out, G1_out, C, D);
  not not_2 (not_2_out, B);
  or G2 (Y2, G1_out, not_1_out, G3_out);
  xnor G6 (Y0, not_2_out, G3_out);
  xnor G4 (Y1, Y0, A);
  xor G5 (Y3, A, Y2, G3_out);
endmodule
