// Logisim project simple-ff.circ as structural Verilog: 2 circuits, main circuit main
module main (
  input  CLK,
  output Q1,
  output Q2
);

  wire FF1_qn, FF2_qn, XOR1_out;

  J_K_Flip_Flop FF1 (.J(Q2), .K(FF2_qn), .clk(CLK), .Q(Q1), .Qn(FF1_qn));  // open: preset, reset
  D_Flip_Flop FF2 (.D(XOR1_out), .clk(CLK), .Q(Q2), .Qn(FF2_qn));  // open: preset, reset
  xor XOR1 (XOR1_out, Q2, FF1_qn);
endmodule

module testbench (
  output [3:0] outval,
  output halt
);

  wire clock_1_out;
  wire [3:0] counter_1_q;

  Clock clock_1 (.out(clock_1_out));
  Counter #(.max('h1f), .width(5)) counter_1 (
    .clk(clock_1_out), .Q({halt, counter_1_q}));  // open: clr, load, up, count, D, carry
  main main_1 (.CLK(clock_1_out), .Q1(outval[0]), .Q2(outval[1]));
endmodule
