// Logisim project 5_bit_adder.circ as structural Verilog: 2 circuits, main circuit main
module main (
  input  A0,
  input  A1,
  input  A2,
  input  A3,
  input  A4,
  input  B0,
  input  B1,
  input  B2,
  input  B3,
  input  B4,
  output S0,
  output S1,
  output S2,
  output S3,
  output S4,
  output S5
);

  Adder #(.width(5)) adder_1 (
    .a({A4, A3, A2, A1, A0}), .b({B4, B3, B2, B1, B0}), .out({S4, S3, S2, S1, S0}), .cout(S5));  // open: cin
endmodule

module main_gates (
  input  A0,
  input  A1,
  input  A2,
  input  A3,
  input  A4,
  input  B0,
  input  B1,
  input  B2,
  input  B3,
  input  B4,
  output S0,
  output S1,
  output S2,
  output S3,
  output S4,
  output S5
);

  wire and_1_out, and_2_out, and_3_out, and_4_out, and_5_out, and_6_out, and_7_out, and_8_out, and_9_out,
       and_10_out, and_11_out, and_12_out, and_13_out, and_14_out, and_15_out, and_16_out, and_17_out,
       and_18_out, and_19_out, and_20_out, and_21_out, and_22_out, and_23_out, and_24_out, and_25_out,
       and_26_out, and_27_out, and_28_out, and_29_out, and_30_out, and_31_out, and_32_out, and_33_out,
       and_34_out, and_35_out, and_36_out, and_37_out, and_38_out, and_39_out, and_40_out, and_41_out,
       and_42_out, and_43_out, and_44_out, and_45_out, and_46_out, and_47_out, and_48_out, and_49_out,
       and_50_out, and_51_out, and_52_out, and_53_out, and_54_out, and_55_out, and_56_out, and_57_out,
       and_58_out, and_59_out, and_60_out, and_61_out, and_62_out, and_63_out, and_64_out, and_65_out,
       and_66_out, and_67_out, and_68_out, and_69_out, and_70_out, and_71_out, and_72_out, and_73_out,
       and_74_out, and_75_out, and_76_out, and_77_out, and_78_out, and_79_out, and_80_out, and_81_out,
       and_82_out, and_83_out, and_84_out, and_85_out, and_86_out, and_87_out, and_88_out, and_89_out,
       and_90_out, and_91_out, and_92_out, and_93_out, and_94_out, and_95_out, and_96_out, and_97_out,
       and_98_out, and_99_out, and_100_out, and_101_out, and_102_out, and_103_out, and_104_out, and_105_out,
       and_106_out, and_107_out, and_108_out, and_109_out, and_110_out, and_111_out, and_112_out,
       and_113_out, and_114_out, and_115_out, and_116_out, and_117_out, and_118_out, and_119_out,
       and_120_out, and_121_out, and_122_out, and_123_out, and_124_out, and_125_out, and_126_out,
       and_127_out, and_128_out, and_129_out, and_130_out, and_131_out, and_132_out, and_133_out,
       and_134_out, and_135_out, and_136_out, and_137_out, and_138_out, and_139_out, and_140_out,
       and_141_out, and_142_out, and_143_out, and_144_out, and_145_out, and_146_out, and_147_out,
       and_148_out, and_149_out, and_150_out, and_151_out, and_152_out, and_153_out, and_154_out,
       and_155_out, and_156_out, and_157_out, and_158_out, and_159_out, and_160_out, and_161_out,
       and_162_out, and_163_out, and_164_out, and_165_out, and_166_out, and_167_out, not_1_out, not_2_out,
       not_3_out, not_4_out, not_5_out, not_6_out, not_7_out, not_8_out, not_9_out, not_10_out, or_6_out,
       or_8_out;

  not not_1 (not_1_out, A0);
  not not_2 (not_2_out, A1);
  not not_3 (not_3_out, A2);
  not not_4 (not_4_out, A3);
  not not_5 (not_5_out, A4);
  not not_6 (not_6_out, B0);
  not not_7 (not_7_out, B1);
  not not_8 (not_8_out, B2);
  not not_9 (not_9_out, B3);
  not not_10 (not_10_out, B4);
  and and_1 (and_1_out, not_1_out, B0);
  and and_2 (and_2_out, A0, not_6_out);
  and and_3 (and_3_out, not_1_out, not_2_out, B1);
  and and_4 (and_4_out, not_1_out, A1, not_7_out);
  and and_5 (and_5_out, not_2_out, not_6_out, B1);
  and and_6 (and_6_out, A0, not_2_out, B0, not_7_out);
  and and_7 (and_7_out, A1, not_6_out, not_7_out);
  and and_8 (and_8_out, A0, A1, B0, B1);
  and and_9 (and_9_out, not_1_out, not_2_out, not_3_out, B2);
  and and_10 (and_10_out, not_1_out, not_2_out, A2, not_8_out);
  and and_11 (and_11_out, A1, not_3_out, B1, not_8_out);
  and and_12 (and_12_out, not_1_out, not_3_out, not_7_out, B2);
  and and_13 (and_13_out, A1, A2, B1, B2);
  and and_14 (and_14_out, not_1_out, A2, not_7_out, not_8_out);
  and and_15 (and_15_out, not_2_out, not_3_out, not_6_out, B2);
  and and_16 (and_16_out, not_2_out, not_3_out, not_7_out, B2);
  and and_17 (and_17_out, A0, not_3_out, B0, B1, not_8_out);
  and and_18 (and_18_out, not_2_out, A2, not_6_out, not_8_out);
  and and_19 (and_19_out, not_2_out, A2, not_7_out, not_8_out);
  and and_20 (and_20_out, A0, A2, B0, B1, B2);
  and and_21 (and_21_out, not_3_out, not_6_out, not_7_out, B2);
  and and_22 (and_22_out, A0, A1, not_3_out, B0, not_8_out);
  and and_23 (and_23_out, A2, not_6_out, not_7_out, not_8_out);
  and and_24 (and_24_out, A0, A1, A2, B0, B2);
  and and_25 (and_25_out, not_1_out, not_2_out, not_3_out, not_4_out, B3);
  and and_26 (and_26_out, not_1_out, not_2_out, not_3_out, A3, not_9_out);
  and and_27 (and_27_out, A2, not_4_out, B2, not_9_out);
  and and_28 (and_28_out, not_1_out, not_2_out, not_4_out, not_8_out, B3);
  and and_29 (and_29_out, A2, A3, B2, B3);
  and and_30 (and_30_out, not_1_out, not_2_out, A3, not_8_out, not_9_out);
  and and_31 (and_31_out, not_3_out, not_4_out, not_8_out, B3);
  and and_32 (and_32_out, A1, not_4_out, B1, B2, not_9_out);
  and and_33 (and_33_out, not_1_out, not_3_out, not_4_out, not_7_out, B3);
  and and_34 (and_34_out, not_3_out, A3, not_8_out, not_9_out);
  and and_35 (and_35_out, A1, A3, B1, B2, B3);
  and and_36 (and_36_out, not_1_out, not_3_out, A3, not_7_out, not_9_out);
  and and_37 (and_37_out, A1, A2, not_4_out, B1, not_9_out);
  and and_38 (and_38_out, not_1_out, not_4_out, not_7_out, not_8_out, B3);
  and and_39 (and_39_out, A1, A2, A3, B1, B3);
  and and_40 (and_40_out, not_1_out, A3, not_7_out, not_8_out, not_9_out);
  and and_41 (and_41_out, not_2_out, not_3_out, not_4_out, not_6_out, B3);
  and and_42 (and_42_out, not_2_out, not_3_out, not_4_out, not_7_out, B3);
  and and_43 (and_43_out, A0, not_4_out, B0, B1, B2, not_9_out);
  and and_44 (and_44_out, not_2_out, not_3_out, A3, not_6_out, not_9_out);
  and and_45 (and_45_out, not_2_out, not_3_out, A3, not_7_out, not_9_out);
  and and_46 (and_46_out, A0, A3, B0, B1, B2, B3);
  and and_47 (and_47_out, not_2_out, not_4_out, not_6_out, not_8_out, B3);
  and and_48 (and_48_out, not_2_out, not_4_out, not_7_out, not_8_out, B3);
  and and_49 (and_49_out, A0, A2, not_4_out, B0, B1, not_9_out);
  and and_50 (and_50_out, not_2_out, A3, not_6_out, not_8_out, not_9_out);
  and and_51 (and_51_out, not_2_out, A3, not_7_out, not_8_out, not_9_out);
  and and_52 (and_52_out, A0, A2, A3, B0, B1, B3);
  and and_53 (and_53_out, not_3_out, not_4_out, not_6_out, not_7_out, B3);
  and and_54 (and_54_out, A0, A1, not_4_out, B0, B2, not_9_out);
  and and_55 (and_55_out, not_3_out, A3, not_6_out, not_7_out, not_9_out);
  and and_56 (and_56_out, A0, A1, A3, B0, B2, B3);
  and and_57 (and_57_out, not_4_out, not_6_out, not_7_out, not_8_out, B3);
  and and_58 (and_58_out, A0, A1, A2, not_4_out, B0, not_9_out);
  and and_59 (and_59_out, A3, not_6_out, not_7_out, not_8_out, not_9_out);
  and and_60 (and_60_out, A0, A1, A2, A3, B0, B3);
  and and_61 (and_61_out, not_1_out, not_2_out, not_3_out, not_4_out, not_5_out, B4);
  and and_62 (and_62_out, not_1_out, not_2_out, not_3_out, not_4_out, A4, not_10_out);
  and and_63 (and_63_out, A3, not_5_out, B3, not_10_out);
  and and_64 (and_64_out, not_1_out, not_2_out, not_3_out, not_5_out, not_9_out, B4);
  and and_65 (and_65_out, A3, A4, B3, B4);
  and and_66 (and_66_out, not_1_out, not_2_out, not_3_out, A4, not_9_out, not_10_out);
  and and_67 (and_67_out, not_4_out, not_5_out, not_9_out, B4);
  and and_68 (and_68_out, A2, not_5_out, B2, B3, not_10_out);
  and and_69 (and_69_out, not_1_out, not_2_out, not_4_out, not_5_out, not_8_out, B4);
  and and_70 (and_70_out, not_4_out, A4, not_9_out, not_10_out);
  and and_71 (and_71_out, A2, A4, B2, B3, B4);
  and and_72 (and_72_out, not_1_out, not_2_out, not_4_out, A4, not_8_out, not_10_out);
  and and_73 (and_73_out, A2, A3, not_5_out, B2, not_10_out);
  and and_74 (and_74_out, not_1_out, not_2_out, not_5_out, not_8_out, not_9_out, B4);
  and and_75 (and_75_out, A2, A3, A4, B2, B4);
  and and_76 (and_76_out, not_1_out, not_2_out, A4, not_8_out, not_9_out, not_10_out);
  and and_77 (and_77_out, not_3_out, not_4_out, not_5_out, not_8_out, B4);
  and and_78 (and_78_out, A1, not_5_out, B1, B2, B3, not_10_out);
  and and_79 (and_79_out, not_1_out, not_3_out, not_4_out, not_5_out, not_7_out, B4);
  and and_80 (and_80_out, not_3_out, not_4_out, A4, not_8_out, not_10_out);
  and and_81 (and_81_out, A1, A4, B1, B2, B3, B4);
  and and_82 (and_82_out, not_1_out, not_3_out, not_4_out, A4, not_7_out, not_10_out);
  and and_83 (and_83_out, not_3_out, not_5_out, not_8_out, not_9_out, B4);
  and and_84 (and_84_out, A1, A3, not_5_out, B1, B2, not_10_out);
  and and_85 (and_85_out, not_1_out, not_3_out, not_5_out, not_7_out, not_9_out, B4);
  and and_86 (and_86_out, not_3_out, A4, not_8_out, not_9_out, not_10_out);
  and and_87 (and_87_out, A1, A3, A4, B1, B2, B4);
  and and_88 (and_88_out, not_1_out, not_3_out, A4, not_7_out, not_9_out, not_10_out);
  and and_89 (and_89_out, A1, A2, not_5_out, B1, B3, not_10_out);
  and and_90 (and_90_out, not_1_out, not_4_out, not_5_out, not_7_out, not_8_out, B4);
  and and_91 (and_91_out, A1, A2, A4, B1, B3, B4);
  and and_92 (and_92_out, not_1_out, not_4_out, A4, not_7_out, not_8_out, not_10_out);
  and and_93 (and_93_out, A1, A2, A3, not_5_out, B1, not_10_out);
  and and_94 (and_94_out, not_1_out, not_5_out, not_7_out, not_8_out, not_9_out, B4);
  and and_95 (and_95_out, A1, A2, A3, A4, B1, B4);
  and and_96 (and_96_out, not_1_out, A4, not_7_out, not_8_out, not_9_out, not_10_out);
  and and_97 (and_97_out, not_2_out, not_3_out, not_4_out, not_5_out, not_6_out, B4);
  and and_98 (and_98_out, not_2_out, not_3_out, not_4_out, not_5_out, not_7_out, B4);
  and and_99 (and_99_out, A0, not_5_out, B0, B1, B2, B3, not_10_out);
  and and_100 (and_100_out, not_2_out, not_3_out, not_4_out, A4, not_6_out, not_10_out);
  and and_101 (and_101_out, not_2_out, not_3_out, not_4_out, A4, not_7_out, not_10_out);
  and and_102 (and_102_out, A0, A4, B0, B1, B2, B3, B4);
  and and_103 (and_103_out, not_2_out, not_3_out, not_5_out, not_6_out, not_9_out, B4);
  and and_104 (and_104_out, not_2_out, not_3_out, not_5_out, not_7_out, not_9_out, B4);
  and and_105 (and_105_out, A0, A3, not_5_out, B0, B1, B2, not_10_out);
  and and_106 (and_106_out, not_2_out, not_3_out, A4, not_6_out, not_9_out, not_10_out);
  and and_107 (and_107_out, not_2_out, not_3_out, A4, not_7_out, not_9_out, not_10_out);
  and and_108 (and_108_out, A0, A3, A4, B0, B1, B2, B4);
  and and_109 (and_109_out, not_2_out, not_4_out, not_5_out, not_6_out, not_8_out, B4);
  and and_110 (and_110_out, not_2_out, not_4_out, not_5_out, not_7_out, not_8_out, B4);
  and and_111 (and_111_out, A0, A2, not_5_out, B0, B1, B3, not_10_out);
  and and_112 (and_112_out, not_2_out, not_4_out, A4, not_6_out, not_8_out, not_10_out);
  and and_113 (and_113_out, not_2_out, not_4_out, A4, not_7_out, not_8_out, not_10_out);
  and and_114 (and_114_out, A0, A2, A4, B0, B1, B3, B4);
  and and_115 (and_115_out, not_2_out, not_5_out, not_6_out, not_8_out, not_9_out, B4);
  and and_116 (and_116_out, not_2_out, not_5_out, not_7_out, not_8_out, not_9_out, B4);
  and and_117 (and_117_out, A0, A2, A3, not_5_out, B0, B1, not_10_out);
  and and_118 (and_118_out, not_2_out, A4, not_6_out, not_8_out, not_9_out, not_10_out);
  and and_119 (and_119_out, not_2_out, A4, not_7_out, not_8_out, not_9_out, not_10_out);
  and and_120 (and_120_out, A0, A2, A3, A4, B0, B1, B4);
  and and_121 (and_121_out, not_3_out, not_4_out, not_5_out, not_6_out, not_7_out, B4);
  and and_122 (and_122_out, A0, A1, not_5_out, B0, B2, B3, not_10_out);
  and and_123 (and_123_out, not_3_out, not_4_out, A4, not_6_out, not_7_out, not_10_out);
  and and_124 (and_124_out, A0, A1, A4, B0, B2, B3, B4);
  and and_125 (and_125_out, not_3_out, not_5_out, not_6_out, not_7_out, not_9_out, B4);
  and and_126 (and_126_out, A0, A1, A3, not_5_out, B0, B2, not_10_out);
  and and_127 (and_127_out, not_3_out, A4, not_6_out, not_7_out, not_9_out, not_10_out);
  and and_128 (and_128_out, A0, A1, A3, A4, B0, B2, B4);
  and and_129 (and_129_out, not_4_out, not_5_out, not_6_out, not_7_out, not_8_out, B4);
  and and_130 (and_130_out, A0, A1, A2, not_5_out, B0, B3, not_10_out);
  and and_131 (and_131_out, not_4_out, A4, not_6_out, not_7_out, not_8_out, not_10_out);
  and and_132 (and_132_out, A0, A1, A2, A4, B0, B3, B4);
  and and_133 (and_133_out, not_5_out, not_6_out, not_7_out, not_8_out, not_9_out, B4);
  and and_134 (and_134_out, A0, A1, A2, A3, not_5_out, B0, not_10_out);
  and and_135 (and_135_out, A4, not_6_out, not_7_out, not_8_out, not_9_out, not_10_out);
  and and_136 (and_136_out, A0, A1, A2, A3, A4, B0, B4);
  and and_137 (and_137_out, A4, B4);
  and and_138 (and_138_out, A3, B3, B4);
  and and_139 (and_139_out, A3, A4, B3);
  and and_140 (and_140_out, A2, B2, B3, B4);
  and and_141 (and_141_out, A2, A4, B2, B3);
  and and_142 (and_142_out, A2, A3, B2, B4);
  and and_143 (and_143_out, A2, A3, A4, B2);
  and and_144 (and_144_out, A1, B1, B2, B3, B4);
  and and_145 (and_145_out, A1, A4, B1, B2, B3);
  and and_146 (and_146_out, A1, A3, B1, B2, B4);
  and and_147 (and_147_out, A1, A3, A4, B1, B2);
  and and_148 (and_148_out, A1, A2, B1, B3, B4);
  and and_149 (and_149_out, A1, A2, A4, B1, B3);
  and and_150 (and_150_out, A1, A2, A3, B1, B4);
  and and_151 (and_151_out, A1, A2, A3, A4, B1);
  and and_152 (and_152_out, A0, B0, B1, B2, B3, B4);
  and and_153 (and_153_out, A0, A4, B0, B1, B2, B3);
  and and_154 (and_154_out, A0, A3, B0, B1, B2, B4);
  and and_155 (and_155_out, A0, A3, A4, B0, B1, B2);
  and and_156 (and_156_out, A0, A2, B0, B1, B3, B4);
  and and_157 (and_157_out, A0, A2, A4, B0, B1, B3);
  and and_158 (and_158_out, A0, A2, A3, B0, B1, B4);
  and and_159 (and_159_out, A0, A2, A3, A4, B0, B1);
  and and_160 (and_160_out, A0, A1, B0, B2, B3, B4);
  and and_161 (and_161_out, A0, A1, A4, B0, B2, B3);
  and and_162 (and_162_out, A0, A1, A3, B0, B2, B4);
  and and_163 (and_163_out, A0, A1, A3, A4, B0, B2);
  and and_164 (and_164_out, A0, A1, A2, B0, B3, B4);
  and and_165 (and_165_out, A0, A1, A2, A4, B0, B3);
  and and_166 (and_166_out, A0, A1, A2, A3, B0, B4);
  and and_167 (and_167_out, A0, A1, A2, A3, A4, B0);
  or or_1 (S0, and_1_out, and_2_out);
  or or_2 (S1, and_3_out, and_4_out, and_5_out, and_6_out, and_7_out, and_8_out);
  or or_3 (S2, and_9_out, and_10_out, and_11_out, and_12_out, and_13_out, and_14_out, and_15_out, and_16_out, and_17_out, and_18_out, and_19_out, and_20_out, and_21_out, and_22_out, and_23_out, and_24_out);
  or or_4 (S3, and_25_out, and_26_out, and_27_out, and_28_out, and_29_out, and_30_out, and_31_out, and_32_out, and_33_out, and_34_out, and_35_out, and_36_out, and_37_out, and_38_out, and_39_out, and_40_out, and_41_out, and_42_out, and_43_out, and_44_out, and_45_out, and_46_out, and_47_out, and_48_out, and_49_out, and_50_out, and_51_out, and_52_out, and_53_out, and_54_out, and_55_out, and_56_out, and_57_out, and_58_out, and_59_out, and_60_out);
  or or_5 (S5, and_137_out, and_138_out, and_139_out, and_140_out, and_141_out, and_142_out, and_143_out, and_144_out, and_145_out, and_146_out, and_147_out, and_148_out, and_149_out, and_150_out, and_151_out, and_152_out, and_153_out, and_154_out, and_155_out, and_156_out, and_157_out, and_158_out, and_159_out, and_160_out, and_161_out, and_162_out, and_163_out, and_164_out, and_165_out, and_166_out, and_167_out);
  or or_6 (or_6_out, and_61_out, and_62_out, and_63_out, and_64_out, and_65_out, and_66_out, and_67_out, and_68_out, and_69_out, and_70_out, and_71_out, and_72_out, and_73_out, and_74_out, and_75_out, and_76_out, and_77_out, and_78_out, and_79_out, and_80_out, and_81_out, and_82_out, and_83_out, and_84_out, and_85_out, and_86_out, and_87_out, and_88_out, and_89_out, and_90_out, and_91_out, and_92_out, and_93_out, and_94_out, and_95_out, and_96_out, and_97_out, and_98_out);
  or or_7 (S4, or_6_out, or_8_out);
  or or_8 (or_8_out, and_99_out, and_100_out, and_101_out, and_102_out, and_103_out, and_104_out, and_105_out, and_106_out, and_107_out, and_108_out, and_109_out, and_110_out, and_111_out, and_112_out, and_113_out, and_114_out, and_115_out, and_116_out, and_117_out, and_118_out, and_119_out, and_120_out, and_121_out, and_122_out, and_123_out, and_124_out, and_125_out, and_126_out, and_127_out, and_128_out, and_129_out, and_130_out, and_131_out, and_132_out, and_133_out, and_134_out, and_135_out, and_136_out);
endmodule
