// Logisim project awful.circ as structural Verilog: 1 circuit, main circuit main
module main (
  input  A,
  input  B,
  input  C,
  input  D,
  input  E,
  input  F,
  output V,
  output Q,
  output R,
  output S,
  output T,
  output U
);

  wire NOR1_out, OR1_out;

  and AND2 (Q, A, B);
  nor NOR1 (NOR1_out, E, F);
  or OR2 (V, Q, OR1_out);
  and AND1 (S, B, D);
  or OR1 (OR1_out, C, S);
  not not_1 (R, NOR1_out);
  nand NAND1 (T, S, R);
  nor NOR2 (U, R, F);
endmodule
