// Logisim project combinatorial.circ as structural Verilog: 1 circuit, main circuit main
module main (
  input  A,
  input  B,
  input  C,
  input  D,
  input  E,
  input  F,
  input  G,
  input  H,
  output Y0,
  output Y1,
  output Y2,
  output Y3,
  output Y4,
  output Y5
);

  wire and_1_out, and_2_out, not_1_out, not_2_out, not_3_out, or_2_out;

  not not_1 (not_1_out, G);
  and and_1 (and_1_out, A, D);
  nand nand_1 (Y5, G, C, B, H);
  not not_2 (not_2_out, E);
  and and_2 (and_2_out, and_1_out, D, not_1_out);
  not not_3 (not_3_out, C);
  or or_1 (Y2, and_1_out, not_2_out, and_2_out);
  xnor xnor_1 (Y0, not_3_out, and_2_out);
  or or_2 (or_2_out, and_2_out, and_1_out, E, Y5);
  xnor xnor_2 (Y1, Y0, A);
  xor xor_1 (Y3, A, Y2, and_2_out, F, or_2_out);
  xnor xnor_3 (Y4, D, A, and_1_out, Y5);
endmodule
