// Logisim project invgates.circ as structural Verilog: 1 circuit, main circuit main
module main (
  input  A,
  input  B,
  input  E,
  input  F,
  output U1,
  output U2,
  output U3,
  output U4,
  output U5,
  output U6,
  output U7,
  output U8,
  output U9,
  output U10,
  output U11,
  output U12,
  output L1,
  output L2,
  output L3,
  output L4,
  output L5,
  output L6,
  output L7,
  output L8
);

  and and_1 (U1, A, B);
  or or_1 (L1, F, E);
  and and_2 (U2, ~A, B);  // AND_Gate
  or or_2 (L2, ~F, E);  // OR_Gate
  and and_3 (U3, A, ~B);  // AND_Gate
  or or_3 (L3, F, ~E);  // OR_Gate
  and and_4 (U4, ~A, ~B);  // AND_Gate
  or or_4 (L4, ~F, ~E);  // OR_Gate
  nand nand_1 (U5, A, B);
  xor xor_1 (L5, F, E);
  nand nand_2 (U6, ~A, B);  // NAND_Gate
  xor xor_2 (L6, ~F, E);  // XOR_Gate
  nand nand_3 (U7, A, ~B);  // NAND_Gate
  xor xor_3 (L7, F, ~E);  // XOR_Gate
  nand nand_4 (U8, ~A, ~B);  // NAND_Gate
  xor xor_4 (L8, ~F, ~E);  // XOR_Gate
  nor nor_1 (U9, A, B);
  nor nor_2 (U10, ~A, B);  // NOR_Gate
  nor nor_3 (U11, A, ~B);  // NOR_Gate
  nor nor_4 (U12, ~A, ~B);  // NOR_Gate
endmodule
