// Logisim project nandgates.circ as structural Verilog: 1 circuit, main circuit main
module main (
  input  A,
  input  B,
  output NW,
  output NM,
  output NN,
  output WW,
  output EW,
  output WM,
  output EM,
  output WN,
  output EN,
  output SN,
  output SM,
  output SW
);

  nand NAND12 (EW, ~A, B);  // NAND_Gate
  nand NAND11 (EM, ~A, B);  // NAND_Gate
  nand NAND10 (EN, ~A, B);  // NAND_Gate
  nand NAND2 (NM, ~A, B);  // NAND_Gate
  nand NAND1 (NN, ~A, B);  // NAND_Gate
  nand NAND9 (SN, ~A, B);  // NAND_Gate
  nand NAND8 (SM, ~A, B);  // NAND_Gate
  nand NAND3 (NW, ~A, B);  // NAND_Gate
  nand NAND7 (SW, ~A, B);  // NAND_Gate
  nand NAND4 (WW, ~A, B);  // NAND_Gate
  nand NAND5 (WM, ~A, B);  // NAND_Gate
  nand NAND6 (WN, ~A, B);  // NAND_Gate
endmodule
