// Logisim project notgatesnake.circ as structural Verilog: 1 circuit, main circuit main
module main (
  input  A,
  output Y
);

  wire not_1_out, not_3_out, not_4_out, not_5_out, not_6_out, not_7_out, not_8_out, not_9_out;

  not not_1 (not_1_out, not_4_out);
  not not_2 (Y, not_3_out);
  not not_3 (not_3_out, not_4_out);
  not not_4 (not_4_out, not_6_out);
  not not_5 (not_5_out, A);
  not not_6 (not_6_out, not_9_out);
  not not_7 (not_7_out, not_5_out);
  not not_8 (not_8_out, not_7_out);
  not not_9 (not_9_out, not_8_out);

  // Notes on the sheet:
  //   I'm a lonely unconnected wire
endmodule
