// Logisim project other_circuit_name.circ as structural Verilog: 1 circuit, main circuit main
module schnubbelwurz (
  input  A,
  input  B
);

  // AND_Gate and_1 has open pins: in0=A, out=open
endmodule
