// Logisim project stateful.circ as structural Verilog: 2 circuits, main circuit main
module main (
  input  CLK,
  output Q1,
  output Q2,
  output Q3,
  output Q4
);

  wire FF1_qn, FF3_qn, FF4_qn, XOR1_out, XOR2_out;

  J_K_Flip_Flop FF1 (.J(Q4), .K(FF4_qn), .clk(CLK), .Q(Q1), .Qn(FF1_qn));  // open: preset, reset
  D_Flip_Flop FF2 (.D(XOR1_out), .clk(CLK), .Q(Q2));  // open: Qn, preset, reset
  xor XOR1 (XOR1_out, Q4, FF1_qn);
  D_Flip_Flop FF3 (.D(Q2), .clk(CLK), .Q(Q3), .Qn(FF3_qn));  // open: preset, reset
  xor XOR2 (XOR2_out, FF3_qn, FF4_qn);
  D_Flip_Flop FF4 (.D(XOR2_out), .clk(CLK), .Q(Q4), .Qn(FF4_qn));  // open: preset, reset
endmodule

module testbench (
  output [3:0] outval,
  output halt
);

  wire clock_1_out;
  wire [3:0] counter_1_q;

  Clock clock_1 (.out(clock_1_out));
  Counter #(.max('h1f), .width(5)) counter_1 (
    .clk(clock_1_out), .Q({halt, counter_1_q}));  // open: clr, load, up, count, D, carry
  main main_1 (.CLK(clock_1_out), .Q1(outval[0]), .Q2(outval[1]), .Q3(outval[2]), .Q4(outval[3]));
endmodule
