// Logisim project undriven_net.circ as structural Verilog: 1 circuit, main circuit main
module main (
  output V,
  output W
);

  // AND_Gate BADBOI has open pins: in0=V, out=open

  assign W = V;

  // Notes on the sheet:
  //   OMG it's not connected
endmodule
