// Logisim project unknown_component.circ as structural Verilog: 1 circuit, main circuit main
module main (
  input  A,
  input  B
);

  // SCHNUBBELWURZ_Gate schnubbelwurz_1: pin names not known; wires that end beside it: A, B
endmodule
