// Logisim project unknown_gate_size.circ as structural Verilog: 1 circuit, main circuit main
module main (
  input  A,
  input  B,
  output Y
);

  // AND_Gate G: pin names not known; wires that end beside it: A, Y, B
endmodule
