// Logisim project widebois.circ as structural Verilog: 1 circuit, main circuit main
module main (
  input  A,
  output Y
);

  wire G1_out, G2_out, G3_out, G4_out;

  or G1 (G1_out, A, ~A, ~A);  // OR_Gate
  and G3 (G3_out, ~G1_out, ~G1_out, G1_out, ~G1_out, ~G1_out);  // AND_Gate
  and G2 (G2_out, ~G1_out, ~G1_out, G1_out, G1_out);  // AND_Gate
  or G4 (G4_out, G2_out, G2_out, ~G2_out, ~G3_out, ~G3_out, ~G3_out);  // OR_Gate
  nand G5 (Y, G2_out, ~G4_out, ~G4_out, G4_out, G4_out, G4_out, ~G4_out);  // NAND_Gate
endmodule
