// Logisim project xorgates.circ as structural Verilog: 1 circuit, main circuit main
module main (
  input  A,
  input  B,
  output NW,
  output NM,
  output NN,
  output WW,
  output EW,
  output WM,
  output EM,
  output WN,
  output EN,
  output SN,
  output SM,
  output SW
);

  xor XOR12 (EW, ~A, B);  // XOR_Gate
  xor XOR11 (EM, ~A, B);  // XOR_Gate
  xor XOR10 (EN, ~A, B);  // XOR_Gate
  xor XOR2 (NM, ~A, B);  // XOR_Gate
  xor XOR1 (NN, ~A, B);  // XOR_Gate
  xor XOR9 (SN, ~A, B);  // XOR_Gate
  xor XOR8 (SM, ~A, B);  // XOR_Gate
  xor XOR3 (NW, ~A, B);  // XOR_Gate
  xor XOR7 (SW, ~A, B);  // XOR_Gate
  xor XOR4 (WW, ~A, B);  // XOR_Gate
  xor XOR5 (WM, ~A, B);  // XOR_Gate
  xor XOR6 (WN, ~A, B);  // XOR_Gate
endmodule
